# Fritzing sketch bham_sensor (saved by Fritzing 0.9.3b)
circuit board: 5.41078cm x 3.79696cm
breadboards: 1

parts:
  temp = Generic male header - 3 pins [form="♂ (male)" package=THT]
  light = Generic double row male header - 2 pins [form="♂ (male)" package=THT]
  particle = male pin header, 6 pins [form="♂ (male)"]
  ard_right = female pin header, 12 pins [form="♀ (female)"]
  ard_left = female pin header, 12 pins [form="♀ (female)"]
  noise = male pin header, 3 pins [form="♂ (male)"]
  330 = Resistor [tolerance=±5% resistance=330 package="0805 [SMD]"]
  100 = Resistor [tolerance=±5% resistance=100 package="0805 [SMD]"]
  100_2 = Resistor [tolerance=±5% resistance=100 package="0805 [SMD]"]
  btn2 = male pin header, 2 pins [form="♂ (male)"]
  btn1 = male pin header, 2 pins [form="♂ (male)"]
  status = RGB LED (com. cathode, rgb) [package="5 mm [THT]"]
  10k = Resistor [tolerance=±5% resistance=10k package="0805 [SMD]"]
  10k_2 = Resistor [tolerance=±5% resistance=10k package="0805 [SMD]"]
  1k = Resistor [tolerance=±5% resistance=1k package="0805 [SMD]"]
  510 = Resistor [tolerance=±5% resistance=510 package="0805 [SMD]"]
  10k_3 = Resistor [tolerance=±5% resistance=10k package="0805 [SMD]"]
  10k_4 = Resistor [tolerance=±5% resistance=10k package="0805 [SMD]"]
  NPN = NPN-Transistor [package="SOT-23 [SMD]"]
  Raspberry_Pi_1 = Raspberry Pi 3 [part_number=RPI-3-V1.2]
  10k1 = Resistor [tolerance=±5% resistance=10k package="0805 [SMD]"]
  10k2 = Resistor [tolerance=±5% resistance=10k package="0805 [SMD]"]
  R1 = Resistor [tolerance=±5% resistance=150 package="0805 [SMD]"]
  C1 = Electrolytic Capacitor [capacitance=220µF package="0405 [SMD, electrolytic]"]

nets:
  5v/dust_vcc: temp.5v, light.in, particle.pin6, ard_right.pin12, noise.pin3, 10k.Pin_1, 10k_3.Pin_1, Raspberry_Pi_1.5V, R1.Pin_1
  temp_dout: temp.d, ard_right.pin5, 10k.Pin_0
  dust_led_gnd/dust_s_gnd/gnd: temp.gnd, particle.pin2, particle.pin4, ard_right.pin11, noise.pin2, 10k_2.Pin_1, 1k.Pin_1, Raspberry_Pi_1.GND, 10k1.Pin_0, 10k2.Pin_0, C1.-
  light_aout: light.out, ard_left.pin1, 10k_2.Pin_0
  dust_v_led: particle.pin1, R1.Pin_0, C1.+
  dust_led: particle.pin3, ard_left.pin10
  dust_v0: particle.pin5, ard_left.pin6
  ard_rx: ard_right.pin2, 10k_3.Pin_0, NPN.1
  ard_tx: ard_right.pin3, 510.Pin_1
  mic_aout: ard_left.pin2, noise.pin1
  status_red: 330.Pin_0, Raspberry_Pi_1.GPIO25
  N1: 330.Pin_1, status.red_anode
  status_green: 100.Pin_0, Raspberry_Pi_1.GPIO24
  N2: 100.Pin_1, status.green_anode
  status_blue: 100_2.Pin_0, Raspberry_Pi_1.GPIO23
  N3: 100_2.Pin_1, status.blue_anode
  sw2: btn2.pin1, Raspberry_Pi_1.GPIO21
  N4: btn2.pin2, 10k2.Pin_1
  sw1: btn1.pin1, Raspberry_Pi_1.GPIO20
  N5: btn1.pin2, 10k1.Pin_1
  status_anode: status.common_cathode, Raspberry_Pi_1.GPIO12
  pi_rx: 1k.Pin_0, 510.Pin_0, Raspberry_Pi_1.GPIO15
  N6: 10k_4.Pin_0, NPN.0
  3v: 10k_4.Pin_1, Raspberry_Pi_1.3v3, Raspberry_Pi_1.3V3
  pi_tx: NPN.2, Raspberry_Pi_1.GPIO14

notes:
  bham city sensor
  rev 1.0
  5v
  d
  gnd
  Vout
  Vled
  led
  Vo
  Vcc
  rx
  3v3
  tx
  11~
  A0
  A4
  A5
  4
  out
  r=gpio25
  g=gpio24
  b=gpio23

custom parts:
  Generic male header - 3 pins: Generic male header
  Generic double row male header - 2 pins: Generic double row male header
